# Fritzing sketch relay (saved by Fritzing 0.9.3b)

parts:
  Raspberry_Pi1 = Raspberry Pi 2
  Componente1 = Logic Level Converter
  KY-1 = Keyes Relay [package=THT]

nets:
  N1: Raspberry_Pi1.3v3, Componente1.LV
  N2: Raspberry_Pi1.GPIO17, Componente1.TX_LV
  GND: Raspberry_Pi1.GND, Componente1.GND, KY-1.ground
  N3: Raspberry_Pi1.5V, Componente1.HV, KY-1.power
  N4: Componente1.TX_HV, KY-1.signal

custom parts:
  Keyes Relay: The Keyes 5V relay module is suitable for SCM development, home appliance control. It uses a 5V~12V TIL control signal which can control DC / AC signal.
